# Fritzing sketch PreciousMetalProbe (saved by Fritzing 1.0.1rc)
circuit board: 11.3733cm x 5.66886cm
breadboards: 1

parts:
  A1 = Waveshare rp2040-zero tht [package=THT]
  U2_TMUX1101 = UNBUFFERED_INVERTER [package=sc70]
  U1_OPA2320 = LTC6244 [package=msop8]
  L1 = Inductor [package="1206 [SMD]"]
  C1 = Ceramic Capacitor [capacitance=100nF voltage=35V package="100 mil [THT, multilayer]"]
  R1 = Resistor [tolerance=±5% resistance=10k package="1206 [SMD]"]
  R2 = Resistor [tolerance=±5% resistance=10k package="1206 [SMD]"]
  R5 = Resistor [tolerance=±5% resistance=100k package="1206 [SMD]"]
  R3 = Resistor [tolerance=±5% resistance=330 package="1206 [SMD]"]

nets:
  N1: A1.Pin_2, U2_TMUX1101.A, U2_TMUX1101.VCC, U1_OPA2320.G$1_+V, R1.Pin_0, R5.Pin_1
  N2: A1.Pin_3, U2_TMUX1101.GND, U1_OPA2320.G$1_-V
  N3: A1.Pin_7, U2_TMUX1101.Y, R5.Pin_0
  N4: U2_TMUX1101.NC, R3.Pin_1
  N5: U1_OPA2320.G$1_OUT, U1_OPA2320.G$1_-IN, L1.pin_1, C1.1
  N6: U1_OPA2320.G$1_+IN, R1.Pin_1, R2.Pin_0
  N7: U1_OPA2320.G$2_+IN, L1.pin_0, C1.0, R3.Pin_0
  N8: U1_OPA2320.G$2_-IN, U1_OPA2320.G$2_OUT

custom parts:
  Waveshare rp2040-zero tht: .RP2040-Zero, A Low-Cost, High-Performance Pico-Like MCU Board Based On Raspberry Pi Microcontroller RP2040. This varant is THT without the extra connections.
